# Fritzing sketch Display System (saved by Fritzing 0.9.3b)
breadboards: 1

parts:
  Part6 = Arduino Uno (Rev3)
  NRF24L6 = NRF24L01
  U4 = Battery Holders [package=lipo-1100mAh]
  TP4 = TP4056 [chip_label=TP4056 package="DIP (Dual Inline) [THT]"]
  Mod2 = generic-ac-power-supply [package=THT]
  Part7 = Display LED de 8 dígitos basado en MAX7219  # not connected
  Part8 = Display LED de 8 dígitos basado en MAX7219  # not connected
  M1 = MAX7219 8x8 single Led Matrix Module
  LED1 = LEDs [package=led10mm]
  KY-1 = Keyes Relay [package=THT]

nets:
  N1: Part6.D8, NRF24L6.CE
  N2: Part6.D9_PWM, NRF24L6.SCK
  N3: Part6.D10_PWM/SS, NRF24L6.MISO
  N4: Part6.D11_PWM/MOSI, KY-1.power
  N5: Part6.D1/TX, M1.I-DIN
  N6: Part6.D2, M1.I-CS
  N7: Part6.D3_PWM, M1.I-CLK
  N8: Part6.D5_PWM, NRF24L6.CSN
  N9: Part6.D6_PWM, NRF24L6.MOSI
  N10: Part6.D7, NRF24L6.IRQ
  N11: Part6.VIN, U4.+, M1.I-VCC, KY-1.signal
  N12: NRF24L6.VCC, TP4.pin3
  N13: U4.-, TP4.pin6, M1.I-GND, KY-1.ground
  N14: TP4.pin1, Mod2.pin3#2
  N15: TP4.pin2, Mod2.pin3#3
  N16: LED1.A, KY-1.NC

custom parts:
  NRF24L01: NRF24L01 module
  TP4056: A DIP stand-in part for whatever IC you want. With 6 pins on a 300mil dual inline package (DIP) footprint.
  generic-ac-power-supply: Generic ac power supply module. Use as is, or customize the svgs to fit your particular device (as they are all different.) Provides AC input and single DC output. PCB is generic and will need modifications if you intend to do a pcb mount.
  MAX7219 8x8 single Led Matrix Module: Description: MAX7219 8x8 LedMatrix single Red Module Dimensions: 32x32mm Documents:
  LEDs: LEDs Standard schematic elements and footprints for 5mm, 3mm, 1206, and 0603 sized LEDs. 5mm - Spark Fun Electronics SKU : COM-00529 (and others)
  Keyes Relay: The Keyes 5V relay module is suitable for SCM development, home appliance control. It uses a 5V~12V TIL control signal which can control DC / AC signal.
