# Fritzing sketch train leaving diagram (saved by Fritzing 0.9.3b)
breadboards: 1

parts:
  Part3 = Arduino Uno (Rev3)
  NRF24L4 = NRF24L01
  e-radionica_com2 = LM393 vibration sensor breakout [part_number=100031]
  U2 = Battery Holders [package=lipo-1100mAh]
  Part4 = Solar Cell
  TP2 = TP4056 [chip_label=TP4056 package="DIP (Dual Inline) [THT]"]

nets:
  N1: Part3.A0, e-radionica_com2.AO
  N2: Part3.D8, NRF24L4.CE
  N3: Part3.D9_PWM, NRF24L4.SCK
  N4: Part3.D10_PWM/SS, NRF24L4.MISO
  N5: Part3.D5_PWM, NRF24L4.CSN
  N6: Part3.D6_PWM, NRF24L4.MOSI
  N7: Part3.D7, NRF24L4.IRQ
  VIN: Part3.VIN, e-radionica_com2.VCC, U2.+
  N8: NRF24L4.VCC, TP2.pin3
  N9: e-radionica_com2.GND, U2.-, TP2.pin6
  N10: Part4.+, TP2.pin1
  N11: Part4.-, TP2.pin2

custom parts:
  NRF24L01: NRF24L01 module
  TP4056: A DIP stand-in part for whatever IC you want. With 6 pins on a 300mil dual inline package (DIP) footprint.
