# Fritzing sketch train reaching diagram (saved by Fritzing 0.9.3b)
breadboards: 1

parts:
  NRF24L1 = NRF24L01
  Part1 = Arduino Uno (Rev3)
  e-radionica_com1 = LM393 vibration sensor breakout [part_number=100031]
  U1 = Battery Holders [package=lipo-1100mAh]
  NRF24L2 = NRF24L01
  Part2 = Solar Cell
  TP1 = TP4056 [chip_label=TP4056 package="DIP (Dual Inline) [THT]"]

nets:
  N1: NRF24L1.VCC, TP1.pin3
  N2: NRF24L1.CSN, Part1.D5_PWM
  N3: NRF24L1.MOSI, Part1.D6_PWM
  N4: NRF24L1.IRQ, Part1.D7
  N5: NRF24L1.CE, Part1.D8
  N6: NRF24L1.SCK, Part1.D9_PWM
  N7: NRF24L1.MISO, Part1.D10_PWM/SS
  N8: Part1.A0, e-radionica_com1.AO
  N9: Part1.D0/RX, NRF24L2.CSN
  N10: Part1.D1/TX, NRF24L2.MOSI
  N11: Part1.D2, NRF24L2.CE
  N12: Part1.D3_PWM, NRF24L2.SCK
  N13: Part1.D4, NRF24L2.MISO
  VCC: Part1.VIN, e-radionica_com1.VCC, U1.+, NRF24L2.VCC
  GND: e-radionica_com1.GND, U1.-, NRF24L2.GND, TP1.pin6
  N14: Part2.+, TP1.pin1
  N15: Part2.-, TP1.pin2

custom parts:
  NRF24L01: NRF24L01 module
  TP4056: A DIP stand-in part for whatever IC you want. With 6 pins on a 300mil dual inline package (DIP) footprint.
