# Fritzing sketch train transmitter (saved by Fritzing 0.9.3b)
breadboards: 1

parts:
  Part5 = Arduino Uno (Rev3)
  NRF24L5 = NRF24L01
  Mod1 = generic-ac-power-supply [package=THT]

nets:
  N1: Part5.D8, NRF24L5.CE
  N2: Part5.D9_PWM, NRF24L5.SCK
  N3: Part5.D10_PWM/SS, NRF24L5.MISO
  N4: Part5.D5_PWM, NRF24L5.CSN
  N5: Part5.D6_PWM, NRF24L5.MOSI
  N6: Part5.D7, NRF24L5.IRQ
  N7: Part5.GND, Mod1.pin3#3
  VIN: Part5.VIN, NRF24L5.VCC, Mod1.pin3#2

custom parts:
  NRF24L01: NRF24L01 module
  generic-ac-power-supply: Generic ac power supply module. Use as is, or customize the svgs to fit your particular device (as they are all different.) Provides AC input and single DC output. PCB is generic and will need modifications if you intend to do a pcb mount.
